# Fritzing sketch ventilastation-esp32s3 (saved by Fritzing 0.9.3b)

parts:
  J30 = double row male pin header, 4 pins [form="♂ (male)"]
  Q4 = NPN-Transistor [package="TO92 [THT]"]
  J31 = male pin header, 3 pins [form="♂ (male)"]
  M1 = MAX485 Breakout [package=THT]
  DOTSTAR1 = DotStar Strip -- Black (60/m) [part_number=2239]
  J33 = screw terminal, 3 pins
  J34 = screw terminal, 3 pins
  C1 = Electrolytic Capacitor [capacitance=100µF voltage=16V package="200 mil [THT, electrolytic]"]
  R1 = Resistor [tolerance=±5% resistance=4.7k package=THT]
  R2 = Resistor [tolerance=±5% resistance=10k package=THT]
  R3 = Resistor [tolerance=±5% resistance=1k package=THT]
  M2 = MAX485 Breakout [package=THT]
  A1 = Werner Rothschopf (modified to ESP32-S3-DevKitC dual USB by vanepp Aug 2024)

nets:
  N1: J30.pin1, Q4.E, J31.pin3, DOTSTAR1.+5V, C1.+
  N2: J30.pin2, DOTSTAR1.CI, A1.Pin_8
  N3: J30.pin3, DOTSTAR1.DI, A1.Pin_9
  N4: J30.pin4, Q4.C, J31.pin2, DOTSTAR1.GND, C1.-
  N5: Q4.B, J31.pin1, R3.Pin_1, A1.Pin_4
  N6: M1.DI, J33.pin1, A1.Pin_16
  N7: J33.pin3, R2.Pin_1, A1.Pin_22
  N8: J34.pin1, A1.Pin_21
  N9: J34.pin3, R1.Pin_0, M2.RO
  N10: R1.Pin_1, R2.Pin_0, A1.Pin_15
  N11: R3.Pin_0, A1.Pin_1, A1.Pin_2

notes:
  A3144 - hall sensor
  107 x APA102 - (144led/m, ipx65)
  1000µF - 16V
  1kΩ
  10kΩ
  4k7
  ESP32-S3
  2 x MAX485

custom parts:
  MAX485 Breakout: MAX485 RS485 breakout board
  DotStar Strip -- Black (60/m): NeopixelDotStar Strip, Black, 60 pixels per meter.
  Werner Rothschopf (modified to ESP32-S3-DevKitC dual USB by vanepp Aug 2024): ESP32-S3 ESP32-S3-DevKitC-1 Dual USB development board Pyboard CircuitPython Micropython wifi BLE5.0 ESP32-S3.
